# Fritzing sketch nodeMCULolin_DHT22m_MHZ19_DM119_b (saved by Fritzing 0.9.4)
circuit board: 5.1191cm x 5.75579cm
breadboards: 2

parts:
  MH-Z19 = MH-Z19 CO2 sensor [part_number=MH-Z19]
  NodeMCU_LoLin = ESP8266 NodeMCU LoLin module
  DHT22 = DHT22 temperature-humidity sensor [form="♂ (male)" part_number=DHT package=THT]
  OLED = OLED 0.96" 128x64 I2C SSD1306
  LED1 = RGB LED (com. cathode, rgb) [package="5 mm [THT]"]
  R1 = Resistor [tolerance=±5% resistance=220 package=THT]
  R2 = Resistor [tolerance=±5% resistance=220 package=THT]
  R3 = Resistor [tolerance=±5% resistance=220 package=THT]
  5V = Camdenboss CTB0158-2 [part_number=Connector package=THT]
  NodeMCU_Amica = female pin header, 15 pins [form="♀ (female)"]
  MG811 = DM-118 [package=THT]

nets:
  GND: MH-Z19.GND, NodeMCU_LoLin.GND, DHT22.GND, OLED.GND, LED1.common_cathode, 5V.pin2, NodeMCU_Amica.pin2, NodeMCU_Amica.pin10, NodeMCU_Amica.pin14, MG811.GND
  D8: MH-Z19.RX, NodeMCU_LoLin.D8
  D7: MH-Z19.TX, NodeMCU_LoLin.D7
  5V: MH-Z19.Vin, NodeMCU_LoLin.Vin, OLED.VCC, 5V.pin1, NodeMCU_Amica.pin15, MG811.VCC
  D0: NodeMCU_LoLin.D0, DHT22.Data
  D1: NodeMCU_LoLin.D1, OLED.SCL
  D2: NodeMCU_LoLin.D2, OLED.SCA
  D3: NodeMCU_LoLin.D3, R3.Pin_0
  D4: NodeMCU_LoLin.D4, R2.Pin_0
  3.3V: NodeMCU_LoLin.3V3, DHT22.VIN, NodeMCU_Amica.pin11
  D5: NodeMCU_LoLin.D5, R1.Pin_0
  N1: NodeMCU_LoLin.RST, NodeMCU_Amica.pin13
  N2: NodeMCU_LoLin.EN, NodeMCU_Amica.pin12
  N3: NodeMCU_LoLin.SK, NodeMCU_Amica.pin9
  N4: NodeMCU_LoLin.S0, NodeMCU_Amica.pin8
  N5: NodeMCU_LoLin.SC, NodeMCU_Amica.pin7
  N6: NodeMCU_LoLin.S1, NodeMCU_Amica.pin6
  N7: NodeMCU_LoLin.S2, NodeMCU_Amica.pin5
  N8: NodeMCU_LoLin.S3, NodeMCU_Amica.pin4
  N9: NodeMCU_LoLin.VU, NodeMCU_Amica.pin3
  A0: NodeMCU_LoLin.A0, NodeMCU_Amica.pin1, MG811.AOut
  N10: LED1.red_anode, R1.Pin_1
  N11: LED1.green_anode, R2.Pin_1
  N12: LED1.blue_anode, R3.Pin_1

notes:
  - +
  VIN 5V

custom parts:
  ESP8266 NodeMCU LoLin module: ESP8266 based NodeMCU
  DHT22 temperature-humidity sensor: The DHT22 is a basic, low-cost digital temperature and humidity sensor. It uses a capacitive humidity sensor and a thermistor to measure the surrounding air, and spits out a digital signal on the data pin (no analog input pins needed). It's fairly simple to use, but requires careful timing to grab data. The only real downside of this sensor is you can only get new data from it once every 2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
  DM-118: Gas Sensor CO2
